# Fritzing sketch Master Design V1 (saved by Fritzing 1.0.6)
circuit board: 6.8cm x 4.5cm

parts:
  ESP32 = ESP32-S3 supermini
  RFID = PN532 Elechouse RFID NFC Module V3

nets:
  ESP_TO_RFID_SDA: ESP32.Pin_6, RFID.SDA
  ESP_TO_RFID_SCL: ESP32.Pin_7, RFID.SCL
  ESP_TO_RFID_IRQ: ESP32.Pin_8, RFID.IRQ
  3.3V: ESP32.Pin_38, RFID.VCC
  GND: ESP32.Pin_39, RFID.GND#1

notes:
  TOMS, PN532 RFID, 1.0
  SMART PHONE
  ↑
  TOMS

custom parts:
  ESP32-S3 supermini: Esp32-S3 Development board ESP32 SuperMini development board ESP32 Development board WiFi Bluetooth.
  PN532 Elechouse RFID NFC Module V3: NFC is a popular technology in recent years. We often heard this work while smart phone company such as Samsung or HTC introduces their latest high-end phones. Almost all the high-end phone in the market support NFC. Near field communication (NFC) is a set of standards for smart phones and similar devices to establish radio communication with each other by touching them together or bringing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
