# Fritzing sketch Slave Design BJT v2.1 (saved by Fritzing 1.0.6)
circuit board: 11cm x 6.5cm

parts:
  PBTN_1 = SWITCH-MOMENTARY-2 [package=tactile-pth]
  R1 = Resistor [tolerance=±5% resistance=10k power=0.25W package=THT]
  S2 = Toggle Switch spst [package=THT]
  RFID = PN532 Elechouse RFID NFC Module V3
  LCD1 = TFT 1.8 inch 160x128 w SD
  BATTERY = LIPO-110mAh [package=lipo-110]
  ESP32 = ESP32-S3 supermini
  Q2 = NPN-Transistor [package="TO92 [THT]"]
  R2 = Resistor [tolerance=±5% power=0.25W resistance=1k package=THT]

nets:
  GND: PBTN_1.1, S2.COM, RFID.GND#1, LCD1.pin2, ESP32.Pin_1, ESP32.Pin_39, Q2.E
  ESP_TO_PUSHBUTTON_1: PBTN_1.2, R1.Pin_1, ESP32.Pin_8
  3.3V: R1.Pin_0, RFID.VCC, LCD1.pin_1, ESP32.Pin_38
  N1: S2.L1, BATTERY.+
  ESP_TO_RFID_SDA: RFID.SDA, ESP32.Pin_6
  ESP_TO_RFID_SCL: RFID.SCL, ESP32.Pin_7
  ESP_TO_RFID_IRQ: RFID.IRQ, ESP32.Pin_9
  ESP_TO_LCD_CS: LCD1.pin3, ESP32.Pin_34
  ESP_TO_LCD_RST: LCD1.pin4, ESP32.Pin_32
  ESP_TO_LCD_A0: LCD1.pin_5, ESP32.Pin_33
  ESP_TO_LCD_SDA: LCD1.pin_6, ESP32.Pin_35
  ESP_TO_LCD_SCLK: LCD1.pin_7, ESP32.Pin_36
  LCD_LED_SWITCH: LCD1.pin_8, Q2.C
  N2: BATTERY.-, ESP32.Pin_2
  ESP_TO_LCD_LED: ESP32.Pin_37, R2.Pin_0
  5V: ESP32.Pin_40
  N3: Q2.B, R2.Pin_1

notes:
  TOMS
  TOMS, Button, 2.0
  TOMS, RFID, 2.0
  TOMS, LCD ST7735S , 2.0
  TOMS, Low-Side BJT 2N3904 Switch , 2.0

custom parts:
  Toggle Switch spst: Toggle Switch single pole single throw
  PN532 Elechouse RFID NFC Module V3: NFC is a popular technology in recent years. We often heard this work while smart phone company such as Samsung or HTC introduces their latest high-end phones. Almost all the high-end phone in the market support NFC. Near field communication (NFC) is a set of standards for smart phones and similar devices to establish radio communication with each other by touching them together or bringing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
  TFT 1.8 inch 160x128 w SD: This is a generic 1.8 tft spi lcd display available on ebay and others. The 1.8" display has 128x160 color pixels and in this version pin names in breadboard (unlike the real board).
  ESP32-S3 supermini: Esp32-S3 Development board ESP32 SuperMini development board ESP32 Development board WiFi Bluetooth.
