# Fritzing sketch Slave Design v1 (saved by Fritzing 1.0.6)
circuit board: 6cm x 6.5cm

parts:
  S1 = SWITCH-MOMENTARY-2 [package=tactile-pth]
  R1 = Resistor [tolerance=±5% resistance=10k power=0.25W package=THT]
  LCD1 = TFT 1.8 inch 160x128 w SD
  A1 = ESP32-S3 supermini
  U1 = LIPO-110mAh [package=lipo-110]

nets:
  GND: S1.1, LCD1.pin2, A1.Pin_1, A1.Pin_39, U1.+
  N1: S1.2, R1.Pin_1, A1.Pin_8
  N2: R1.Pin_0, A1.Pin_40
  N3: LCD1.pin_1, A1.Pin_38
  N4: LCD1.pin3, A1.Pin_34
  N5: LCD1.pin4, A1.Pin_32
  N6: LCD1.pin_5, A1.Pin_33
  N7: LCD1.pin_6, A1.Pin_35
  N8: LCD1.pin_7, A1.Pin_36
  N9: LCD1.pin_8, A1.Pin_37
  N10: A1.Pin_2, U1.-

notes:
  TOMS

custom parts:
  TFT 1.8 inch 160x128 w SD: This is a generic 1.8 tft spi lcd display available on ebay and others. The 1.8" display has 128x160 color pixels and in this version pin names in breadboard (unlike the real board).
  ESP32-S3 supermini: Esp32-S3 Development board ESP32 SuperMini development board ESP32 Development board WiFi Bluetooth.
