# Fritzing sketch Slave Design v2 (saved by Fritzing 1.0.6)
circuit board: 6cm x 6.5cm

parts:
  S1 = SWITCH-MOMENTARY-2 [package=tactile-pth]
  R1 = Resistor [tolerance=±5% resistance=10k power=0.25W package=THT]
  LCD1 = TFT 1.8 inch 160x128 w SD
  U1 = LIPO-110mAh [package=lipo-110]
  A1 = ESP32-S3 supermini
  Q1 = TRANSISTOR_NPN [package=to-92]  # not connected
  S2 = Toggle Switch spst [package=THT]
  U2 = RFID RC522 SIP - 8 pins [chip_label="RFID RC522" package="SIP (Single Inline) [THT]"]  # not connected

nets:
  GND: S1.1, LCD1.pin2, A1.Pin_1, A1.Pin_39, S2.COM
  N1: S1.2, R1.Pin_1, A1.Pin_8
  3.3V: R1.Pin_0, A1.Pin_38
  5V: LCD1.pin_1, A1.Pin_40
  ESP_TO_LCD_CS: LCD1.pin3, A1.Pin_34
  ESP_TO_LCD_RST: LCD1.pin4, A1.Pin_32
  ESP_TO_LCD_A0: LCD1.pin_5, A1.Pin_33
  ESP_TO_LCD_SDA: LCD1.pin_6, A1.Pin_35
  ESP_TO_LCD_SCLK: LCD1.pin_7, A1.Pin_36
  ESP_TO_LCD_LED: LCD1.pin_8, A1.Pin_37
  N2: U1.+, S2.L1
  N3: U1.-, A1.Pin_2

notes:
  TOMS

custom parts:
  TFT 1.8 inch 160x128 w SD: This is a generic 1.8 tft spi lcd display available on ebay and others. The 1.8" display has 128x160 color pixels and in this version pin names in breadboard (unlike the real board).
  ESP32-S3 supermini: Esp32-S3 Development board ESP32 SuperMini development board ESP32 Development board WiFi Bluetooth.
  Toggle Switch spst: Toggle Switch single pole single throw
  RFID RC522 SIP - 8 pins: A SIP stand-in part for RFID RC522 . With 8 pins on a 300 mil single inline package (SIP) footprint.
